// Logisim project ALU Design.circ as structural Verilog: 3 circuits, main circuit main
module main (
  input  [3:0] rs,
  input  [3:0] rt,
  input  Cin,
  input  [3:0] write_register,
  input  [15:0] write_data,
  input  WC,
  input  CLEAR,
  input  [1:0] ALU_select,
  output [15:0] Read_Data_1,
  output [15:0] Read_Data_2,
  output [15:0] ALU_result,
  output Cout
);

  wire clk_out;

  Clock clk (.out(clk_out));
  _16_bit_RF u_16_bit_rf_1 (
    .Write_Data(write_data), .Write_Register(write_register), .WC(WC), .Clock(clk_out), .CLEAR(CLEAR),
    .Read_Data_1(Read_Data_1), .rs(rs), .Read_Data_2(Read_Data_2), .rt(rt));
  _16_bit_ALU u_16_bit_alu_1 (
    .ALU_select(ALU_select), .MUX_output(ALU_result), .Cout(Cout), .Cin(Cin), .A(Read_Data_1), .B(Read_Data_2));

  // Notes on the sheet:
  //   Name: A. M. A Sakhiur Rahman
  //   ID: 2231507642
endmodule

module _16_bit_RF (
  input  [15:0] Write_Data,
  input  [3:0] rs,
  input  [3:0] Write_Register,
  input  [3:0] rt,
  input  WC,
  input  Clock,
  input  CLEAR,
  output [15:0] Read_Data_1,
  output [15:0] Read_Data_2
);

  wire and_1_out, and_2_out, and_3_out, and_4_out, and_5_out, and_6_out, and_7_out, and_8_out, and_9_out,
       and_10_out, and_11_out, and_12_out, and_13_out, and_14_out, and_15_out, and_16_out, decoder_1_out0,
       decoder_1_out1, decoder_1_out2, decoder_1_out3, decoder_1_out4, decoder_1_out5, decoder_1_out6,
       decoder_1_out7, decoder_1_out8, decoder_1_out9, decoder_1_out10, decoder_1_out11, decoder_1_out12,
       decoder_1_out13, decoder_1_out14, decoder_1_out15;
  wire [15:0] R0_q, R1_q, R2_q, R3_q, R4_q, R5_q, R6_q, R7_q, R8_q, R9_q, R10_q, R11_q, R12_q, R13_q, R14_q,
       R15_q;

  Decoder #(.select(4), .enable("false")) decoder_1 (
    .out0(decoder_1_out0), .out1(decoder_1_out1), .out2(decoder_1_out2), .out3(decoder_1_out3),
    .out4(decoder_1_out4), .out5(decoder_1_out5), .out6(decoder_1_out6), .out7(decoder_1_out7),
    .out8(decoder_1_out8), .out9(decoder_1_out9), .out10(decoder_1_out10), .out11(decoder_1_out11),
    .out12(decoder_1_out12), .out13(decoder_1_out13), .out14(decoder_1_out14), .out15(decoder_1_out15),
    .sel(Write_Register));
  and and_1 (and_1_out, decoder_1_out0, WC);
  and and_2 (and_2_out, decoder_1_out1, WC);
  and and_3 (and_3_out, decoder_1_out2, WC);
  and and_4 (and_4_out, decoder_1_out3, WC);
  and and_5 (and_5_out, decoder_1_out4, WC);
  and and_6 (and_6_out, decoder_1_out5, WC);
  and and_7 (and_7_out, decoder_1_out6, WC);
  and and_8 (and_8_out, decoder_1_out7, WC);
  Register #(.width(16)) R0 (.D(Write_Data), .en(and_1_out), .Q(R0_q), .clk(Clock));  // open: clr
  Register #(.width(16)) R1 (.D(Write_Data), .en(and_2_out), .Q(R1_q), .clk(Clock), .clr(CLEAR));
  Register #(.width(16)) R2 (.D(Write_Data), .en(and_3_out), .Q(R2_q), .clk(Clock), .clr(CLEAR));
  Register #(.width(16)) R3 (.D(Write_Data), .en(and_4_out), .Q(R3_q), .clk(Clock), .clr(CLEAR));
  Register #(.width(16)) R4 (.D(Write_Data), .en(and_5_out), .Q(R4_q), .clk(Clock), .clr(CLEAR));
  Register #(.width(16)) R5 (.D(Write_Data), .en(and_6_out), .Q(R5_q), .clk(Clock), .clr(CLEAR));
  Register #(.width(16)) R6 (.D(Write_Data), .en(and_7_out), .Q(R6_q), .clk(Clock), .clr(CLEAR));
  Register #(.width(16)) R7 (.D(Write_Data), .en(and_8_out), .Q(R7_q), .clk(Clock), .clr(CLEAR));
  and and_9 (and_9_out, decoder_1_out8, WC);
  and and_10 (and_10_out, decoder_1_out9, WC);
  and and_11 (and_11_out, decoder_1_out10, WC);
  and and_12 (and_12_out, decoder_1_out11, WC);
  and and_13 (and_13_out, decoder_1_out12, WC);
  and and_14 (and_14_out, decoder_1_out13, WC);
  and and_15 (and_15_out, decoder_1_out14, WC);
  and and_16 (and_16_out, decoder_1_out15, WC);
  Register #(.width(16)) R8 (.D(Write_Data), .en(and_9_out), .Q(R8_q), .clk(Clock), .clr(CLEAR));
  Register #(.width(16)) R9 (.D(Write_Data), .en(and_10_out), .Q(R9_q), .clk(Clock), .clr(CLEAR));
  Register #(.width(16)) R10 (.D(Write_Data), .en(and_11_out), .Q(R10_q), .clk(Clock), .clr(CLEAR));
  Register #(.width(16)) R11 (.D(Write_Data), .en(and_12_out), .Q(R11_q), .clk(Clock), .clr(CLEAR));
  Register #(.width(16)) R12 (.D(Write_Data), .en(and_13_out), .Q(R12_q), .clk(Clock), .clr(CLEAR));
  Register #(.width(16)) R13 (.D(Write_Data), .en(and_14_out), .Q(R13_q), .clk(Clock), .clr(CLEAR));
  Register #(.width(16)) R14 (.D(Write_Data), .en(and_15_out), .Q(R14_q), .clk(Clock), .clr(CLEAR));
  Register #(.width(16)) R15 (.D(Write_Data), .en(and_16_out), .Q(R15_q), .clk(Clock), .clr(CLEAR));
  Multiplexer #(.select(4), .width(16), .enable("false")) multiplexer_1 (
    .in0(R0_q), .in1(R1_q), .in2(R2_q), .in3(R3_q), .in4(R4_q), .in5(R5_q), .in6(R6_q), .in7(R7_q),
    .in8(R8_q), .in9(R9_q), .in10(R10_q), .in11(R11_q), .in12(R12_q), .in13(R13_q), .in14(R14_q),
    .in15(R15_q), .out(Read_Data_1), .sel(rs));
  Multiplexer #(.select(4), .width(16), .enable("false")) multiplexer_2 (
    .in0(R0_q), .in1(R1_q), .in2(R2_q), .in3(R3_q), .in4(R4_q), .in5(R5_q), .in6(R6_q), .in7(R7_q),
    .in8(R8_q), .in9(R9_q), .in10(R10_q), .in11(R11_q), .in12(R12_q), .in13(R13_q), .in14(R14_q),
    .in15(R15_q), .out(Read_Data_2), .sel(rt));

  // Notes on the sheet:
  //   Name: A.M. A Sakhiur Rahman
  //   ID: 2231507642
endmodule

module _16_bit_ALU (
  input  Cin,
  input  [15:0] A,
  input  [15:0] B,
  input  [1:0] ALU_select,
  output [15:0] MUX_output,
  output Cout
);

  wire [15:0] adder_1_out, and_1_out, multiplexer_1_out, not_1_out, or_1_out;

  Multiplexer #(.width(16), .enable("false")) multiplexer_1 (
    .in0(B), .in1(not_1_out), .out(multiplexer_1_out), .sel(ALU_select[0]));
  assign not_1_out = ~B;  // NOT_Gate not_1, 16 bits wide
  assign and_1_out = A & B;  // AND_Gate and_1, 16 bits wide
  assign or_1_out = A | B;  // OR_Gate or_1, 16 bits wide
  Adder #(.width(16)) adder_1 (.a(A), .b(multiplexer_1_out), .out(adder_1_out), .cin(Cin), .cout(Cout));
  Multiplexer #(.select(2), .width(16), .enable("false")) multiplexer_2 (
    .in0(and_1_out), .in1(or_1_out), .in2(adder_1_out), .in3(adder_1_out), .out(MUX_output), .sel(ALU_select));

  // Notes on the sheet:
  //   Name: A. M. A Sakhiur Rahman
  //   ID: 2231507642
endmodule
