// Logisim project Lab-5 16-bit Register File.circ as structural Verilog: 1 circuit, main circuit main
module main (
  input  [15:0] Write_Data,
  input  [3:0] rs,
  input  [3:0] Write_Register,
  input  [3:0] rd,
  input  WC,
  input  Clock,
  input  CLEAR,
  output [15:0] Read_Data_1,
  output [15:0] Read_Data_2
);

  wire and_1_out, and_2_out, and_3_out, and_4_out, and_5_out, and_6_out, and_7_out, and_8_out, and_9_out,
       and_10_out, and_11_out, and_12_out, and_13_out, and_14_out, and_15_out, and_16_out, decoder_1_out0,
       decoder_1_out1, decoder_1_out2, decoder_1_out3, decoder_1_out4, decoder_1_out5, decoder_1_out6,
       decoder_1_out7, decoder_1_out8, decoder_1_out9, decoder_1_out10, decoder_1_out11, decoder_1_out12,
       decoder_1_out13, decoder_1_out14, decoder_1_out15;
  wire [15:0] R0_q, R1_q, R2_q, R3_q, R4_q, R5_q, R6_q, R7_q, R8_q, R9_q, R10_q, R11_q, R12_q, R13_q, R14_q,
       R15_q;

  Decoder #(.select(4), .enable("false")) decoder_1 (
    .out0(decoder_1_out0), .out1(decoder_1_out1), .out2(decoder_1_out2), .out3(decoder_1_out3),
    .out4(decoder_1_out4), .out5(decoder_1_out5), .out6(decoder_1_out6), .out7(decoder_1_out7),
    .out8(decoder_1_out8), .out9(decoder_1_out9), .out10(decoder_1_out10), .out11(decoder_1_out11),
    .out12(decoder_1_out12), .out13(decoder_1_out13), .out14(decoder_1_out14), .out15(decoder_1_out15),
    .sel(Write_Register));
  and and_1 (and_1_out, decoder_1_out0, WC);
  and and_2 (and_2_out, decoder_1_out1, WC);
  and and_3 (and_3_out, decoder_1_out2, WC);
  and and_4 (and_4_out, decoder_1_out3, WC);
  and and_5 (and_5_out, decoder_1_out4, WC);
  and and_6 (and_6_out, decoder_1_out5, WC);
  and and_7 (and_7_out, decoder_1_out6, WC);
  and and_8 (and_8_out, decoder_1_out7, WC);
  Register #(.width(16)) R0 (.D(Write_Data), .en(and_1_out), .Q(R0_q), .clk(Clock));  // open: clr
  Register #(.width(16)) R1 (.D(Write_Data), .en(and_2_out), .Q(R1_q), .clk(Clock), .clr(CLEAR));
  Register #(.width(16)) R2 (.D(Write_Data), .en(and_3_out), .Q(R2_q), .clk(Clock), .clr(CLEAR));
  Register #(.width(16)) R3 (.D(Write_Data), .en(and_4_out), .Q(R3_q), .clk(Clock), .clr(CLEAR));
  Register #(.width(16)) R4 (.D(Write_Data), .en(and_5_out), .Q(R4_q), .clk(Clock), .clr(CLEAR));
  Register #(.width(16)) R5 (.D(Write_Data), .en(and_6_out), .Q(R5_q), .clk(Clock), .clr(CLEAR));
  Register #(.width(16)) R6 (.D(Write_Data), .en(and_7_out), .Q(R6_q), .clk(Clock), .clr(CLEAR));
  Register #(.width(16)) R7 (.D(Write_Data), .en(and_8_out), .Q(R7_q), .clk(Clock), .clr(CLEAR));
  and and_9 (and_9_out, decoder_1_out8, WC);
  and and_10 (and_10_out, decoder_1_out9, WC);
  and and_11 (and_11_out, decoder_1_out10, WC);
  and and_12 (and_12_out, decoder_1_out11, WC);
  and and_13 (and_13_out, decoder_1_out12, WC);
  and and_14 (and_14_out, decoder_1_out13, WC);
  and and_15 (and_15_out, decoder_1_out14, WC);
  and and_16 (and_16_out, decoder_1_out15, WC);
  Register #(.width(16)) R8 (.D(Write_Data), .en(and_9_out), .Q(R8_q), .clk(Clock), .clr(CLEAR));
  Register #(.width(16)) R9 (.D(Write_Data), .en(and_10_out), .Q(R9_q), .clk(Clock), .clr(CLEAR));
  Register #(.width(16)) R10 (.D(Write_Data), .en(and_11_out), .Q(R10_q), .clk(Clock), .clr(CLEAR));
  Register #(.width(16)) R11 (.D(Write_Data), .en(and_12_out), .Q(R11_q), .clk(Clock), .clr(CLEAR));
  Register #(.width(16)) R12 (.D(Write_Data), .en(and_13_out), .Q(R12_q), .clk(Clock), .clr(CLEAR));
  Register #(.width(16)) R13 (.D(Write_Data), .en(and_14_out), .Q(R13_q), .clk(Clock), .clr(CLEAR));
  Register #(.width(16)) R14 (.D(Write_Data), .en(and_15_out), .Q(R14_q), .clk(Clock), .clr(CLEAR));
  Register #(.width(16)) R15 (.D(Write_Data), .en(and_16_out), .Q(R15_q), .clk(Clock), .clr(CLEAR));
  Multiplexer #(.select(4), .width(16), .enable("false")) multiplexer_1 (
    .in0(R0_q), .in1(R1_q), .in2(R2_q), .in3(R3_q), .in4(R4_q), .in5(R5_q), .in6(R6_q), .in7(R7_q),
    .in8(R8_q), .in9(R9_q), .in10(R10_q), .in11(R11_q), .in12(R12_q), .in13(R13_q), .in14(R14_q),
    .in15(R15_q), .out(Read_Data_1), .sel(rs));
  Multiplexer #(.select(4), .width(16), .enable("false")) multiplexer_2 (
    .in0(R0_q), .in1(R1_q), .in2(R2_q), .in3(R3_q), .in4(R4_q), .in5(R5_q), .in6(R6_q), .in7(R7_q),
    .in8(R8_q), .in9(R9_q), .in10(R10_q), .in11(R11_q), .in12(R12_q), .in13(R13_q), .in14(R14_q),
    .in15(R15_q), .out(Read_Data_2), .sel(rd));

  // Notes on the sheet:
  //   Name: A.M. A Sakhiur Rahman
  //   ID: 2231507642
endmodule
